# Fritzing sketch layout (saved by Fritzing 0.8.0b)
breadboards: 1

parts:
  Part1 = Arduino Uno (Rev3)
  LED1 = LED - 5mm [color="Red (633nm)" package="5 mm [THT]"]
  LED2 = LED - 5mm [color="Red (633nm)" package="5 mm [THT]"]
  LED3 = LED - 5mm [color="Red (633nm)" package="5 mm [THT]"]
  LED4 = LED - 5mm [color="Yellow (595nm)" package="5 mm [THT]"]
  LED5 = LED - 5mm [color="Yellow (595nm)" package="5 mm [THT]"]
  LED6 = LED - 5mm [color="Yellow (595nm)" package="5 mm [THT]"]
  S1 = Pushbutton [package="[THT]"]
  R1 = Resistor [tolerance=±5% resistance=10k package=THT]
  R3 = Rotary Potentiometer (Small)
  LED8 = RGB LED (com. anode, rbg) [package="5 mm [THT]"]

nets:
  N1: Part1.A0, R3.wiper
  N2: Part1.ICSP_MOSI, Part1.D11_PWM/MOSI, LED8.green_cathode
  N3: Part1.D8, S1.Pin_1, S1.Pin_2, R1.Pin_0
  N4: Part1.D9_PWM, LED8.red_cathode
  N5: Part1.D10_PWM/SS, LED8.common_anode
  N6: Part1.D2, LED1.anode
  N7: Part1.D3_PWM, LED3.anode
  N8: Part1.D4, LED2.anode
  N9: Part1.D5_PWM, LED5.anode
  N10: Part1.D6_PWM, LED6.anode
  N11: Part1.D7, LED4.anode
  N12: Part1.5V, S1.Pin_3, S1.Pin_4, R3.leg2
  N13: Part1.GND, R1.Pin_1
  N14: LED1.cathode, LED2.cathode, LED3.cathode, LED4.cathode, LED5.cathode, LED6.cathode, R3.leg1, LED8.blue_cathode
